# Fritzing sketch 70cm-LPF_dl7bst (saved by Fritzing 0.9.2b)
circuit board: 3cm x 3cm
breadboards: 1

parts:
  C3 = Ceramic Capacitor [capacitance=1nF package="100 mil [THT, multilayer]"]
  R1 = Resistor [tolerance=±5% resistance=220 package=THT]
  C1 = Variable Capacitor [capacitance=100nF max_capacitance=10pF min_capacitance=2.1pF voltage=35V]
  C2 = Ceramic Capacitor [capacitance=22pF package="100 mil [THT, multilayer]"]
  ANT = Antenna
  J1 = double row female pin header, 20 pins [form="♀ (female)"]
  L1 = Inductor [inductance=22nH package="1206 [SMD]"]

nets:
  N1: C3.0, C1.1, L1.pin_0
  N2: C3.1, R1.Pin_1
  N3: R1.Pin_0, J1.pin16
  GND: C1.0, C2.0, J1.pin17
  N4: C2.1, ANT.antenna_lead, L1.pin_1

notes:
  RPiTX
  RPiTX LPF 70cm
  Vorwiderstand zur Strombegrenzung
  Wert abhängig vom Mut - kann man auch weglassen
  70cm LPF
  Pin spacing und Lochdurchmesser des VariCap stimmt nicht
