# Fritzing sketch 70cm-LPF_dl7bst_v3 (saved by Fritzing 0.9.2b)
circuit board: 3cm x 2cm
breadboards: 1

parts:
  C2 = CAP_ADJ [part_number=6-30pF package=ctz3]
  U1 = U.FL [package=u.fl]
  L1 = Inductor [inductance=22nH package="1206 [SMD]"]
  C1 = Ceramic Capacitor [capacitance=1nF package="100 mil [THT, multilayer]"]
  R1 = Resistor [tolerance=±5% resistance=220 package=THT]
  ANT = Antenna
  C3 = Ceramic Capacitor [capacitance=22pF package="100 mil [THT, multilayer]"]
  J1 = double row female pin header, 12 pins [form="♀ (female)"]

nets:
  N1: C2.3, L1.pin_0, C1.0
  GND: C2.4, U1.GND, C3.0, J1.pin8
  N2: U1.SIGNAL, L1.pin_1, ANT.antenna_lead, C3.1
  N3: C1.1, R1.Pin_1
  N4: R1.Pin_0, J1.pin6

notes:
  Vorwiderstand zur Strombegrenzung
  Wert abhängig vom Mut - kann man auch weglassen
  RPiTX LPF 70cm
  70cm LPF
  RPiTX
