# Fritzing sketch 70cm-LPF_dl7bst_v3_SMD (saved by Fritzing 0.9.2b)
circuit board: 3.5cm x 2.2cm
breadboards: 1

parts:
  C2 = CAP_ADJ [part_number=6-30pF package=ctz3]
  L1 = Inductor [inductance=22nH package="1206 [SMD]"]
  J1 = double row female pin header, 12 pins [form="♀ (female)"]
  R1 = Resistor [tolerance=±5% resistance=220 package="1206 [SMD]"]
  C1 = Ceramic Capacitor [capacitance=1nF package="1206 [SMD, multilayer]"]
  ANT = U.FL [package=u.fl]
  C3 = Ceramic Capacitor [capacitance=22pF package="1206 [SMD, multilayer]"]
  Pad1 = Pad [width=4 height=2 connect=center]  # not connected
  Pad2 = Pad [width=4 height=2 connect=center]  # not connected
  Pad3 = Pad [width=2 height=4 connect=center]  # not connected
  Pad5 = Pad [width=2 height=2 connect=center]  # not connected
  Pad6 = Pad [width=2 height=2 connect=center]  # not connected
  Pad7 = Pad [width=2 height=2 connect=center]  # not connected
  Pad8 = Pad [width=2 height=2 connect=center]  # not connected
  Pad14 = Pad [width=2 height=4 connect=center]  # not connected

nets:
  N1: C2.3, L1.pin_0, C1.0
  GND: C2.4, J1.pin8, ANT.GND, C3.0
  N2: L1.pin_1, ANT.SIGNAL, C3.1
  N3: J1.pin6, R1.Pin_0
  N4: R1.Pin_1, C1.1

notes:
  Vorwiderstand zur Strombegrenzung
  Wert abhängig vom Mut - kann man auch weglassen
