# Fritzing sketch NotBeleuchtung (saved by Fritzing 0.9.0b)
circuit board: 4.96723cm x 5.19042cm
breadboards: 1

parts:
  Q1 = NPN-Transistor [package="TO92 [THT]"]
  LED1 = LED - 5mm [color="Red (633nm)" package="5 mm [THT]"]
  Q2 = NPN-Transistor [package="TO92 [THT]"]
  VCC1 = 4 x AAA Battery Mount [part_number=6V]
  R2 = Resistor [tolerance=±5% resistance=47 package=THT]
  LED2 = LED - 5mm [color="Red (633nm)" package="5 mm [THT]"]
  R1 = Resistor [tolerance=±5% resistance=22k package=THT]

nets:
  N1: Q1.E, Q2.E, VCC1.-
  N2: Q1.B, LED1.cathode
  N3: Q1.C, Q2.B, R1.Pin_1
  N4: LED1.anode, R2.Pin_0, LED2.anode
  N5: Q2.C, LED2.cathode
  N6: VCC1.+, R2.Pin_1, R1.Pin_0
