# Fritzing sketch Kurzwellendetektor (saved by Fritzing 0.9.0b)
breadboards: 1

parts:
  L1 = Inductor [part_number="5 Windugen" package="400 mil [THT]"]
  L2 = Inductor [part_number="5 Windugen" package="400 mil [THT]"]
  L3 = Inductor [part_number="5 Windugen" package="400 mil [THT]"]
  L4 = Inductor [part_number="5 Windugen" package="400 mil [THT]"]
  L5 = Inductor [part_number="5 Windugen" package="400 mil [THT]"]
  C1 = CAP_ADJ [part_number=240pF package=ctz3]
  C2 = CAP_ADJ [part_number=80pF package=ctz3]
  J1 = Piezo Speaker [part_number=Lautsprecher]
  D1 = Diode [package=diode-1n4001]
  ANT1 = Antenna [part_number=Antenne]

nets:
  N1: L1.pin_0, C1.3, C2.3
  N2: L1.pin_1, L2.pin_0, D1.A
  N3: L2.pin_1, L3.pin_0
  N4: L3.pin_1, L4.pin_0, ANT1.antenna_lead
  N5: L4.pin_1, L5.pin_0
  GND: L5.pin_1, C1.4, C2.4, J1.pin2
  N6: J1.pin1, D1.C
