# Fritzing sketch NPN-Darlington_DL7BST (saved by Fritzing 0.9.0b)

parts:
  BC_547C = NPN-Transistor [part_number=Q1 package="TO92 [THT]"]
  BC_547C_2 = NPN-Transistor [part_number=Q2 package="TO92 [THT]"]
  LED = LED - 5mm [color="Red (633nm)" package="5 mm [THT]"]

nets:
  N1: BC_547C.E, BC_547C_2.B
  finger: BC_547C.B
  N2: BC_547C.C, BC_547C_2.C, LED.cathode
  GND: BC_547C_2.E
  6V: LED.anode

notes:
  U
  in
