# Fritzing sketch NPN-AF-Amp_DL7BST_SchemToBb (saved by Fritzing 0.9.0b)
breadboards: 1

parts:
  SP1 = SPEAKER [package=pcb_mount_speaker]
  BC_547C = NPN-Transistor [package="TO92 [THT]"]
  R2 = Resistor [tolerance=±5% resistance=47 package=THT]
  C1 = Ceramic Capacitor [capacitance="100 nF" package="0603 [SMD, multilayer]"]
  R1 = Resistor [tolerance=±5% resistance=22k package=THT]

nets:
  6V: SP1.+
  N1: SP1.-, R2.Pin_1
  GND: BC_547C.E
  N2: BC_547C.B, C1.1, R1.Pin_0
  N3: BC_547C.C, R2.Pin_0, R1.Pin_1
  signal: C1.0
