# Fritzing sketch 30m-LPF_dl7bst (saved by Fritzing 0.9.3b)
circuit board: 4cm x 3cm
breadboards: 1

parts:
  R1 = Resistor [tolerance=±5% resistance=220 package=THT]
  R2 = Resistor [tolerance=±5% resistance=47 package=THT]
  Q1 = NPN-Transistor [package="TO92 [THT]"]
  L1 = Inductor [inductance=0.1µH package="400 mil [THT]"]
  C1 = Ceramic Capacitor [capacitance=4.7nF package="100 mil [THT, multilayer]"]
  C2 = Ceramic Capacitor [capacitance=4.7nF package="100 mil [THT, multilayer]"]
  C3 = Ceramic Capacitor [capacitance=4.7nF package="100 mil [THT, multilayer]"]
  J1 = double row female pin header, 20 pins [form="♀ (female)"]
  C4 = Ceramic Capacitor [capacitance=100nF package="100 mil [THT, multilayer]"]
  U1 = U.FL [package=u.fl]

nets:
  N1: R1.Pin_0, J1.pin17
  N2: R1.Pin_1, Q1.B
  N3: R2.Pin_0, Q1.E, C1.0
  GND: R2.Pin_1, C2.0, C3.0, J1.pin16, C4.0, U1.GND
  N4: Q1.C, J1.pin20, C4.1
  N5: L1.pin_0, C1.1, C2.1
  N6: L1.pin_1, C3.1, U1.SIGNAL

notes:
  DL7BST
