# Fritzing sketch Fritzing-Demo (saved by Fritzing 0.9.2b)
circuit board: 8.46667cm x 5.64444cm
stripboards: 1

parts:
  JP1 = Header 2 [package=jst-2-pth]
  C1 = Ceramic Capacitor [capacitance=100nF package="100 mil [THT, multilayer]"]
  R1 = Resistor [tolerance=±5% resistance=22k package=THT]
  R2 = Resistor [tolerance=±5% resistance=47 package=THT]
  SP1 = SPEAKER [package=pcb_mount_speaker]
  VCC1 = Battery
  Q1 = NPN-Transistor [package="TO92 [THT]"]
  U1 = Voltage Regulator - 5V [package="TO220 [THT]"]

nets:
  N1: JP1.1, C1.1
  GND: JP1.2, VCC1.+, Q1.E, U1.GND
  N2: C1.0, R1.Pin_0, Q1.B
  N3: R1.Pin_1, R2.Pin_0, Q1.C
  N4: R2.Pin_1, SP1.-
  N5: SP1.+, VCC1.-

notes:
  Audioverstäker, Dollet Ding
  meins
