# Fritzing sketch NotBeleuchtung (saved by Fritzing 0.9.0b)
circuit board: 4.96723cm x 5.19042cm
breadboards: 1

parts:
  R1 = Resistor [tolerance=±5% resistance=1k package=THT]
  Q1 = NPN-Transistor [package="TO92 [THT]"]
  LED2 = LED - 5mm [color="Red (633nm)" package="5 mm [THT]"]
  LED1 = LED - 5mm [color="Red (633nm)" package="5 mm [THT]"]
  VCC1 = Battery block 9V
  Q2 = NPN-Transistor [package="TO92 [THT]"]

nets:
  N1: R1.Pin_0, LED2.anode, LED1.anode, VCC1.+
  N2: R1.Pin_1, Q1.C, Q2.B
  N3: Q1.E, VCC1.-, Q2.E
  N4: Q1.B, LED1.cathode
  N5: LED2.cathode, Q2.C
