# Fritzing sketch NPN-AF-Amp_DL7BST_BbToSchem (saved by Fritzing 0.9.0b)
breadboards: 1

parts:
  C1 = Ceramic Capacitor [capacitance="100 nF" package="0603 [SMD, multilayer]"]
  BC_547C = NPN-Transistor [package="TO92 [THT]"]
  R1 = Resistor [tolerance=±5% resistance=22k package=THT]
  R2 = Resistor [tolerance=±5% resistance=47 package=THT]
  SP1 = SPEAKER [package=pcb_mount_speaker]
  VCC_6V = 4 x AAA Battery Mount

nets:
  signal: C1.0
  N1: C1.1, BC_547C.B, R1.Pin_1
  N2: BC_547C.E, VCC_6V.-
  N3: BC_547C.C, R1.Pin_0, R2.Pin_0
  N4: R2.Pin_1, SP1.+
  N5: SP1.-, VCC_6V.+
