# Fritzing sketch Uebung1 (saved by Fritzing 0.9.2b)
breadboards: 1

parts:
  R1 = Resistor [tolerance=±5% resistance=470 package=THT]
  R2 = Resistor [tolerance=±5% resistance=510 package=THT]
  R3 = Resistor [tolerance=±5% resistance=470 package=THT]
  R4 = Resistor [tolerance=±5% resistance=510 package=THT]
  V1 = DC Power [voltage=6V]

nets:
  N1: R1.Pin_0, R2.Pin_0, R3.Pin_0, R4.Pin_0, V1.V+
  N2: R1.Pin_1, R2.Pin_1, R3.Pin_1, R4.Pin_1, V1.V-

notes:
  A
  B
  C
  D
