# Fritzing sketch Uebung1 (saved by Fritzing 0.9.2b)
breadboards: 1

parts:
  R1 = Resistor [tolerance=±5% resistance=180 package=THT]
  LED1 = LED - 5mm [color="Green (570nm)" package="5 mm [THT]"]
  LED2 = LED - 5mm [color="Red (633nm)" package="5 mm [THT]"]
  C1 = Electrolytic Capacitor [capacitance=1µF package="100 mil [THT, electrolytic]"]
  S1 = Pushbutton [package="[THT]"]
  V1 = DC Power [voltage=6V]

nets:
  N1: R1.Pin_0, S1.Pin_3, S1.Pin_4, V1.V+
  N2: R1.Pin_1, LED1.cathode, LED2.anode
  N3: LED1.anode, LED2.cathode, C1.+
  N4: C1.-, S1.Pin_1, S1.Pin_2, V1.V-
